// Logisim project BRANKAS_DIGITAL.circ as structural Verilog: 4 circuits, main circuit main
module main (
  input  [3:0] DIGIT_1,
  input  [3:0] DIGIT_2,
  input  [3:0] DIGIT_3,
  input  [3:0] DIGIT_4
);

  wire blok_1_verifikasi_1_out_kode, blok_2_penghitung_salah_1_out_alarm, blok_3_alarm_output_1_out_alarm,
       blok_3_alarm_output_1_out_buka, blok_3_alarm_output_1_out_kunci, blok_3_alarm_output_1_out_reset,
       TOMBOL_ENTER_out, TOMBOL_RESET_out;
  wire [3:0] blok_3_alarm_output_1_out_layar;

  Button TOMBOL_ENTER (.out(TOMBOL_ENTER_out));
  Button TOMBOL_RESET (.out(TOMBOL_RESET_out));
  BLOK_1_VERIFIKASI blok_1_verifikasi_1 (
    .DIGIT_1(DIGIT_1), .DIGIT_2(DIGIT_2), .DIGIT_3(DIGIT_3), .DIGIT_4(DIGIT_4),
    .OUT_KODE(blok_1_verifikasi_1_out_kode));
  BLOK_2_PENGHITUNG_SALAH blok_2_penghitung_salah_1 (
    .IN_RESET(blok_3_alarm_output_1_out_reset), .IN_KODE(blok_1_verifikasi_1_out_kode),
    .IN_ENTER(TOMBOL_ENTER_out), .OUT_ALARM(blok_2_penghitung_salah_1_out_alarm));
  BLOK_3_ALARM_OUTPUT blok_3_alarm_output_1 (
    .IN_KODE(blok_1_verifikasi_1_out_kode), .IN_ALARM(blok_2_penghitung_salah_1_out_alarm),
    .IN_RESET(TOMBOL_RESET_out), .OUT_LAYAR(blok_3_alarm_output_1_out_layar),
    .OUT_BUKA(blok_3_alarm_output_1_out_buka), .OUT_KUNCI(blok_3_alarm_output_1_out_kunci),
    .OUT_ALARM(blok_3_alarm_output_1_out_alarm), .OUT_RESET(blok_3_alarm_output_1_out_reset));
  Hex_Digit_Display hex_digit_display_1 (.value(blok_3_alarm_output_1_out_layar));  // open: dp
  LED LED_BRANKAS_TERBUKA (.in(blok_3_alarm_output_1_out_buka));
  LED LED_BRANKAS_TERKUNCI (.in(blok_3_alarm_output_1_out_kunci));
  LED LED_ALARM_AKTIF (.in(blok_3_alarm_output_1_out_alarm));

  // Notes on the sheet:
  //   C = CLOSE (BRANKAS TERKUNCI)
  //   O = OPEN (BRANKAS TERBUKA)
  //   E = ERROR (3X GAGAL INPUT PIN)
endmodule

module BLOK_1_VERIFIKASI (
  input  [3:0] DIGIT_1,
  input  [3:0] DIGIT_2,
  input  [3:0] DIGIT_3,
  input  [3:0] DIGIT_4,
  output OUT_KODE
);

  wire comparator_1_eq, comparator_2_eq, comparator_3_eq, comparator_4_eq;

  Comparator #(.mode("unsigned"), .width(4)) comparator_1 (
    .a(DIGIT_1), .b(4'b0001), .eq(comparator_1_eq));  // open: gt, lt
  Comparator #(.mode("unsigned"), .width(4)) comparator_2 (
    .a(DIGIT_2), .b(4'b0010), .eq(comparator_2_eq));  // open: gt, lt
  Comparator #(.mode("unsigned"), .width(4)) comparator_3 (
    .a(DIGIT_3), .b(4'b0011), .eq(comparator_3_eq));  // open: gt, lt
  Comparator #(.mode("unsigned"), .width(4)) comparator_4 (
    .a(DIGIT_4), .b(4'b0100), .eq(comparator_4_eq));  // open: gt, lt
  and and_1 (OUT_KODE, comparator_1_eq, comparator_2_eq, comparator_3_eq, comparator_4_eq);
endmodule

module BLOK_2_PENGHITUNG_SALAH (
  input  IN_RESET,
  input  IN_KODE,
  input  IN_ENTER,
  output OUT_ALARM
);

  wire not_1_out;
  wire [1:0] counter_1_q;

  not not_1 (not_1_out, IN_KODE);
  Counter #(.max('h3), .ongoal("stay"), .width(2)) counter_1 (
    .clr(IN_RESET), .load(1'b0), .up(1'b1), .count(not_1_out), .clk(IN_ENTER), .Q(counter_1_q));  // open: D, carry
  Comparator #(.mode("unsigned"), .width(2)) comparator_1 (.a(counter_1_q), .b(2'b11), .eq(OUT_ALARM));  // open: gt, lt
endmodule

module BLOK_3_ALARM_OUTPUT (
  input  IN_KODE,
  input  IN_ALARM,
  input  IN_RESET,
  output [3:0] OUT_LAYAR,
  output OUT_BUKA,
  output OUT_KUNCI,
  output OUT_ALARM,
  output OUT_RESET
);

  wire clock_1_out, not_1_out, not_2_out;

  not not_1 (not_1_out, IN_ALARM);
  Clock #(.highDuration(200), .lowDuration(200)) clock_1 (.out(clock_1_out));
  Multiplexer #(.select(2), .width(4)) multiplexer_1 (
    .in0(4'b1100), .in1(4'b0000), .in2(4'b1110), .in3(4'b1110), .out(OUT_LAYAR), .sel({IN_ALARM, IN_KODE}));
  and and_1 (OUT_BUKA, IN_KODE, not_1_out);
  not not_2 (not_2_out, IN_KODE);
  and and_2 (OUT_KUNCI, not_2_out, not_1_out);
  and and_3 (OUT_ALARM, ~not_1_out, ~clock_1_out);  // AND_Gate

  assign OUT_RESET = IN_RESET;
endmodule
